# Fritzing sketch 06ActZumbador (saved by Fritzing 0.9.3b)

parts:
  Arduino = Arduino Uno (Rev3)
  J1 = Piezo Speaker

nets:
  N1: Arduino.D12/MISO, J1.pin2
  N2: Arduino.GND, J1.pin1

// code stored in the sketch: Lec5DigInputs.ino
//www.elegoo.com
//2016.12.08

int ledPin = 5;
int buttonApin = 9;
int buttonBpin = 8;

byte leds = 0;

void setup() 
{
  pinMode(ledPin, OUTPUT);
  pinMode(buttonApin, INPUT_PULLUP);  
  pinMode(buttonBpin, INPUT_PULLUP);  
}

void loop() 
{
  if (digitalRead(buttonApin) == LOW)
  {
    digitalWrite(ledPin, HIGH);
  }
  if (digitalRead(buttonBpin) == LOW)
  {
    digitalWrite(ledPin, LOW);
  }
}

// code stored in the sketch: Lec6ActZumbador.ino
//www.elegoo.com
//2016.12.08

int buzzer = 12;//the pin of the active buzzer
void setup()
{
 pinMode(buzzer,OUTPUT);//initialize the buzzer pin as an output
}
void loop()
{
 unsigned char i;
 while(1)
 {
   //output an frequency
   for(i=0;i<80;i++)
   {
    digitalWrite(buzzer,HIGH);
    delay(1);//wait for 1ms
    digitalWrite(buzzer,LOW);
    delay(1);//wait for 1ms
    }
    //output another frequency
     for(i=0;i<100;i++)
      {
        digitalWrite(buzzer,HIGH);
        delay(2);//wait for 2ms
        digitalWrite(buzzer,LOW);
        delay(2);//wait for 2ms
      }
  }
}
