# Fritzing sketch 07ZumbadorPas (saved by Fritzing 0.9.6b)

parts:
  Arduino = Arduino Uno (Rev3)
  Buzzer = Piezo Speaker

nets:
  N1: Arduino.D8, Buzzer.pin2
  N2: Arduino.GND, Buzzer.pin1

// code stored in the sketch: Lec5DigInputs.ino
//www.elegoo.com
//2016.12.08

int ledPin = 5;
int buttonApin = 9;
int buttonBpin = 8;

byte leds = 0;

void setup() 
{
  pinMode(ledPin, OUTPUT);
  pinMode(buttonApin, INPUT_PULLUP);  
  pinMode(buttonBpin, INPUT_PULLUP);  
}

void loop() 
{
  if (digitalRead(buttonApin) == LOW)
  {
    digitalWrite(ledPin, HIGH);
  }
  if (digitalRead(buttonBpin) == LOW)
  {
    digitalWrite(ledPin, LOW);
  }
}

// code stored in the sketch: Lec7ZumbadorPas.ino
//www.elegoo.com
//2016.12.08

#include "pitches.h"
 
// notes in the melody:
int melody[] = {
  NOTE_C5, NOTE_D5, NOTE_E5, NOTE_F5, NOTE_G5, NOTE_A5, NOTE_B5, NOTE_C6};
int duration = 500;  // 500 miliseconds
 
void setup() {
 
}
 
void loop() {  
  for (int thisNote = 0; thisNote < 8; thisNote++) {
    // pin8 output the voice, every scale is 0.5 sencond
    tone(8, melody[thisNote], duration);
     
    // Output the voice after several minutes
    delay(1000);
  }
   
  // restart after two seconds 
  delay(2000);
}
