# Fritzing sketch 08.InterruptorBolaInclinacion (saved by Fritzing 0.9.6b)
circuit board: 8.46667cm x 5.64444cm
breadboards: 1

parts:
  Componente1 = Arduino Uno (Rev3) - ICSP
  S1 = Tilt Switch [package=THT]
  R5 = Resistor [resistance=220 tolerance=±5% power=0.25 package=THT]
  LED3 = LED - 5mm [color="Red (633nm)" current=0.030 package="5 mm [THT]"]

nets:
  N1: Componente1.GND, S1.Pin_1, LED3.cathode
  N2: Componente1.D13/SCK, R5.Pin_1
  N3: Componente1.D2, S1.Pin_2
  N4: R5.Pin_0, LED3.anode

// code stored in the sketch: 08.InterruptorBolaInclinacionFritzing.ino
/*
 Name:		_08.ino
 Created:	3/20/2021 11:13:59 AM
 Author:	Juan Bustos
*/

const int ledPin = 13;//the led attach to

void setup()
{ 
  pinMode(ledPin,OUTPUT);//initialize the ledPin as an output
  pinMode(2,INPUT);
  digitalWrite(2, HIGH);
} 

void loop() 
{ 
  int digitalVal = digitalRead(2); //read pin 2
  if(HIGH == digitalVal)
  {
    digitalWrite(ledPin,LOW);//turn the led off
  }
  else
  {
    digitalWrite(ledPin,HIGH);//turn the led on 
  }
}
