# Fritzing sketch 09.ServoFritzing (saved by Fritzing 0.9.6b)
circuit board: 5.64444cm x 8.46667cm
breadboards: 1

parts:
  Arduino1 = Arduino Uno (Rev3)
  M1 = Dagu DGServo 9g (Top view) [part_number=RS001B]

nets:
  N1: Arduino1.D9_PWM, M1.pulse
  5V: Arduino1.5V, M1.vcc
  GND: Arduino1.GND, M1.gnd

// code stored in the sketch: 09.ServoFritzing.ino
#include <Servo.h>
/* After including the corresponding libraries,
   we can use the "class" like "Servo" created by the developer for us.
   We can use the functions and variables created in the libraries by creating 
   objects like the following "myservo" to refer to the members in ".".*/

Servo myservo;
//it created an object called myservo.
/*  you can see Servo as a complex date type(Including functions and various data types)
    and see myservo as variables.               */

void setup(){
  /*"attach" and "write" are both functions,
     and they are members contained in the complex structure of "Servo". 
     We can only use them if we create the object "myservo" for the complex structure of "Servo".
  */
  myservo.attach(9);//connect pin 9 with the control line(the middle line of Servo) 
  myservo.write(90);// move servos to center position -> 90°
} 
void loop(){
  myservo.write(90);// move servos to center position -> 90°
  delay(1000);
  myservo.write(60);// move servos to center position -> 60°
  delay(1000);
  myservo.write(90);// move servos to center position -> 90°
  delay(1000);
  myservo.write(150);// move servos to center position -> 120°
  delay(1000);
}
