# Fritzing sketch 10.SensorUltrasonico (saved by Fritzing 0.9.6b)
circuit board: 8.46667cm x 5.64444cm
breadboards: 1

parts:
  Componente1 = Arduino Uno (Rev3) - ICSP
  HC-SR04_Sensor_1 = HC-SR04 Ultrasonic Distance Sensor

nets:
  N1: Componente1.ICSP_MOSI, Componente1.D11_PWM/MOSI, Componente1.D12/MISO, HC-SR04_Sensor_1.TRIG, HC-SR04_Sensor_1.ECHO
  5V: Componente1.5V, HC-SR04_Sensor_1.VCC
  GND: Componente1.GND, HC-SR04_Sensor_1.GND

// code stored in the sketch: 10SensorUltrasonicoFritzing.ino
//www.elegoo.com
//2016.12.08
#include "SR04.h"

#define TRIG_PIN 12
#define ECHO_PIN 11 

SR04 sr04 = SR04(ECHO_PIN,TRIG_PIN);
long a;

void setup() {
   Serial.begin(9600);//Initialization of Serial Port
   delay(1000);
}

void loop() {
   a=sr04.Distance();
   Serial.print(a);
   Serial.println("cm");//The difference between "Serial.print" and "Serial.println" 
                        //is that "Serial.println" can change lines.
   delay(1000);
}
