# Fritzing sketch 12.JoystickAnalogico (saved by Fritzing 0.9.6b)
circuit board: 8.46667cm x 5.64444cm
breadboards: 1

parts:
  Componente1 = Arduino Uno (Rev3) - ICSP
  Mod1 = KY-023 Dual Axis Joystick Module [package="Breakout board"]

nets:
  N1: Componente1.A0, Mod1.VRx
  N2: Componente1.A1, Mod1.VRy
  N3: Componente1.D2, Mod1.SW
  5V: Componente1.5V, Mod1.+5V
  GND: Componente1.GND, Mod1.GND

custom parts:
  KY-023 Dual Axis Joystick Module: KY-023 Dual-Axis Joystick Module.

// code stored in the sketch: 12.JoystickAnalogicoFritzing.fzz.ino
// Arduino pin numbers
const int SW_pin = 2; // digital pin connected to switch output
const int X_pin = 0; // analog pin connected to X output
const int Y_pin = 1; // analog pin connected to Y output

void setup() {
  pinMode(SW_pin, INPUT);
  digitalWrite(SW_pin, HIGH);
  Serial.begin(9600);
}

void loop() {
  Serial.print("Switch:  ");
  Serial.print(digitalRead(SW_pin));
  Serial.print("\n");
  Serial.print("X-axis: ");
  Serial.print(analogRead(X_pin));
  Serial.print("\n");
  Serial.print("Y-axis: ");
  Serial.println(analogRead(Y_pin));
  Serial.print("\n\n");
  delay(1000);
}
