# Fritzing sketch 13.ReceptorIR (saved by Fritzing 0.9.6b)
circuit board: 8.46667cm x 5.64444cm
breadboards: 1

parts:
  Mod1 = KY-022 Infrared Receiver Module [package="Breakout board"]
  Componente1 = Arduino Uno (Rev3)

nets:
  N1: Mod1.-, Componente1.GND
  VIN: Mod1.Vin, Componente1.5V
  N2: Mod1.S, Componente1.D11_PWM/MOSI

custom parts:
  KY-022 Infrared Receiver Module: KY-022 IR receiver module, reacts to 38kHz infrared light.

// code stored in the sketch: 13.ReceptorIRFritzing.ino
//www.elegoo.com
//2020.3.12

#include "IRremote.h"
#include "IR.h"

IRrecv irrecv(RECEIVER);     // create instance of 'irrecv'
decode_results results;      // create instance of 'decode_results'

void setup() {
  Serial.begin(9600);
  Serial.println("IR Receiver Button Decode");
  irrecv.enableIRIn();
}

void loop()
{
  int tmpValue;
  if (irrecv.decode(&results)) // have we received an IR signal?
  {
    for (int i = 0; i < 23; i++)
    {
      if ((keyValue[i] == results.value) && (i<KEY_NUM))
      {
        Serial.println(keyBuf[i]);
        tmpValue = results.value;
      }
      else if(REPEAT==i)
      {
        results.value = tmpValue;
      }
    }
    irrecv.resume(); // receive the next value
  }


//The implementation effect of the above program is 
//the same as that of the following, but it is more concise

//    switch(results.value)
//  {
//  case 0xFFA25D: Serial.println("POWER"); break;
//  case 0xFFE21D: Serial.println("FUNC/STOP"); break;
//  case 0xFF629D: Serial.println("VOL+"); break;
//  case 0xFF22DD: Serial.println("FAST BACK");    break;
//  case 0xFF02FD: Serial.println("PAUSE");    break;
//  case 0xFFC23D: Serial.println("FAST FORWARD");   break;
//  case 0xFFE01F: Serial.println("DOWN");    break;
//  case 0xFFA857: Serial.println("VOL-");    break;
//  case 0xFF906F: Serial.println("UP");    break;
//  case 0xFF9867: Serial.println("EQ");    break;
//  case 0xFFB04F: Serial.println("ST/REPT");    break;
//  case 0xFF6897: Serial.println("0");    break;
//  case 0xFF30CF: Serial.println("1");    break;
//  case 0xFF18E7: Serial.println("2");    break;
//  case 0xFF7A85: Serial.println("3");    break;
//  case 0xFF10EF: Serial.println("4");    break;
//  case 0xFF38C7: Serial.println("5");    break;
//  case 0xFF5AA5: Serial.println("6");    break;
//  case 0xFF42BD: Serial.println("7");    break;
//  case 0xFF4AB5: Serial.println("8");    break;
//  case 0xFF52AD: Serial.println("9");    break;
//  case 0xFFFFFFFF: Serial.println(" REPEAT");break;  
//  default: 
//    Serial.println(" other button   ");

//  }// End Case
}
